// Logisim project alu.circ as structural Verilog: 13 circuits, main circuit Main circuit
module Main_circuit (
  input  in_1,
  input  in_2,
  input  in_3,
  input  in_4,
  input  in_5,
  input  in_6,
  input  in_7,
  input  in_8,
  input  in_9,
  input  in_10,
  output out_11,
  output out_12,
  output out_13,
  output out_14,
  output out_15,
  output out_16,
  output out_17,
  output out_18,
  output out_19,
  output out_20,
  output out_21,
  output out_22,
  output out_23,
  output out_24,
  output out_25,
  output out_26,
  output out_27,
  output out_28,
  output out_29,
  output out_30,
  output out_31,
  output out_32,
  output out_33,
  output out_34,
  output out_35,
  output out_36,
  output out_37,
  output out_38,
  output out_39,
  output out_40,
  output out_41,
  output out_42,
  output out_43,
  output out_44,
  output out_45,
  output out_46,
  output out_47,
  output out_48,
  output out_49,
  output out_50
);

  _4_Bit_comparator u_4_bit_comparator_1 (
    .A0(in_1), .B0(in_5), .A1(in_2), .B1(in_6), .A2(in_3), .B2(in_7), .A3(in_4), .B3(in_8), .out_9(out_32),
    .out_10(out_33), .out_11(out_34));
  Bitsie_or bitsie_or_1 (
    .A3(in_8), .B3(in_4), .A2(in_7), .B2(in_3), .A1(in_6), .B1(in_2), .A0(in_5), .B0(in_1), .out_9(out_39),
    .out_10(out_40), .out_11(out_41), .out_12(out_42));
  Bitwise_not bitwise_not_1 (
    .in_1(in_5), .in_2(in_6), .in_3(in_7), .in_4(in_8), .out_5(out_47), .out_6(out_48), .out_7(out_49),
    .out_8(out_50));
  Right_shift right_shift_1 (
    .in_2(in_1), .in_3(in_2), .in_4(in_3), .in_5(in_4), .out_6(out_28), .out_7(out_29), .out_8(out_30),
    .out_9(out_31), .in_1(in_10));
  _4_Bit_Multiplier u_4_bit_multiplier_1 (
    .A0(in_1), .B0(in_5), .A1(in_2), .B1(in_6), .A2(in_3), .B2(in_7), .A3(in_4), .B3(in_8), .out_9(out_16),
    .out_10(out_17), .out_11(out_18), .out_12(out_19), .out_13(out_20), .out_14(out_21), .out_15(out_22),
    .out_16(out_23));
  Left_Shift left_shift_1 (
    .in_2(in_1), .in_3(in_2), .in_4(in_3), .in_5(in_4), .out_6(out_24), .out_7(out_25), .out_8(out_26),
    .out_9(out_27), .in_1(in_10));
  Bitwise_and bitwise_and_1 (
    .A3(in_4), .B3(in_6), .A2(in_3), .B2(in_8), .A1(in_7), .B1(in_2), .A0(in_5), .B0(in_1), .out_9(out_38),
    .out_10(out_35), .out_11(out_36), .out_12(out_37));
  Bitwise_xor bitwise_xor_1 (
    .A3(in_8), .B3(in_4), .A2(in_7), .B2(in_3), .A1(in_6), .B1(in_2), .A0(in_5), .B0(in_1), .out_9(out_43),
    .out_10(out_44), .out_11(out_45), .out_12(out_46));
  _4_bit_adder_subtractor u_4_bit_adder_subtractor_1 (
    .A0(in_1), .B0(in_5), .C0(in_9), .A1(in_2), .B1(in_6), .A2(in_3), .B2(in_7), .A3(in_4), .B3(in_8),
    .out_10(out_11), .out_11(out_12), .out_12(out_13), .out_13(out_14), .out_14(out_15));
endmodule

module _4_bit_adder_subtractor (
  input  A0,
  input  B0,
  input  C0,
  input  A1,
  input  B1,
  input  A2,
  input  B2,
  input  A3,
  input  B3,
  output out_10,
  output out_11,
  output out_12,
  output out_13,
  output out_14
);

  wire full_adder_1_out_5, full_adder_2_out_5, full_adder_3_out_5, xor_1_out, xor_2_out, xor_3_out, xor_4_out;

  xor xor_1 (xor_1_out, B0, C0);
  xor xor_2 (xor_2_out, B1, C0);
  xor xor_3 (xor_3_out, C0, B2);
  xor xor_4 (xor_4_out, C0, B3);
  full_adder full_adder_1 (.in_1(A0), .in_2(C0), .in_3(xor_1_out), .out_4(out_10), .out_5(full_adder_1_out_5));
  full_adder full_adder_2 (
    .in_1(A1), .in_2(xor_2_out), .in_3(full_adder_1_out_5), .out_4(out_11), .out_5(full_adder_2_out_5));
  full_adder full_adder_3 (
    .in_1(A2), .in_2(xor_3_out), .in_3(full_adder_2_out_5), .out_4(out_12), .out_5(full_adder_3_out_5));
  full_adder full_adder_4 (.in_1(A3), .in_2(xor_4_out), .in_3(full_adder_3_out_5), .out_4(out_13), .out_5(out_14));
endmodule

module full_adder (
  input  in_1,
  input  in_2,
  input  in_3,
  output out_4,
  output out_5
);

  wire and_1_out, and_2_out, xor_1_out;

  xor xor_1 (xor_1_out, in_1, in_2);
  and and_1 (and_1_out, in_1, in_2);
  xor xor_2 (out_4, xor_1_out, in_3);
  and and_2 (and_2_out, xor_1_out, in_3);
  xor xor_3 (out_5, and_2_out, and_1_out);
endmodule

module Half_adder (
  input  in_1,
  input  in_2,
  output out_3,
  output out_4
);

  xor xor_1 (out_3, in_1, in_2);
  and and_1 (out_4, in_1, in_2);
endmodule

module _4_Bit_Multiplier (
  input  A0,
  input  B0,
  input  A1,
  input  B1,
  input  A2,
  input  B2,
  input  A3,
  input  B3,
  output out_9,
  output out_10,
  output out_11,
  output out_12,
  output out_13,
  output out_14,
  output out_15,
  output out_16
);

  wire and_2_out, and_3_out, and_4_out, and_5_out, and_6_out, and_7_out, and_8_out, and_9_out, and_10_out,
       and_11_out, and_12_out, and_13_out, and_14_out, and_15_out, and_16_out, full_adder_1_out_5,
       full_adder_2_out_4, full_adder_2_out_5, full_adder_3_out_4, full_adder_3_out_5, full_adder_4_out_5,
       full_adder_5_out_4, full_adder_5_out_5, full_adder_6_out_4, full_adder_6_out_5, full_adder_7_out_5,
       half_adder_1_out_4, half_adder_2_out_3, half_adder_2_out_4, half_adder_3_out_3, half_adder_3_out_4,
       half_adder_4_out_4;

  and and_1 (out_9, A0, B0);
  and and_2 (and_2_out, A1, B0);
  and and_3 (and_3_out, A0, B1);
  and and_4 (and_4_out, A2, B0);
  and and_5 (and_5_out, A1, B1);
  and and_6 (and_6_out, A0, B2);
  and and_7 (and_7_out, A3, B0);
  and and_8 (and_8_out, A2, B1);
  and and_9 (and_9_out, A1, B2);
  and and_10 (and_10_out, A0, B3);
  and and_11 (and_11_out, A3, B1);
  and and_12 (and_12_out, A2, B2);
  and and_13 (and_13_out, A1, B3);
  and and_14 (and_14_out, A3, B2);
  and and_15 (and_15_out, A2, B3);
  and and_16 (and_16_out, A3, B3);
  full_adder full_adder_1 (
    .in_1(half_adder_2_out_3), .in_2(and_6_out), .in_3(half_adder_1_out_4), .out_4(out_11),
    .out_5(full_adder_1_out_5));
  full_adder full_adder_2 (
    .in_1(and_7_out), .in_2(and_8_out), .in_3(half_adder_2_out_4), .out_4(full_adder_2_out_4),
    .out_5(full_adder_2_out_5));
  Half_adder half_adder_1 (.in_1(and_2_out), .in_2(and_3_out), .out_3(out_10), .out_4(half_adder_1_out_4));
  Half_adder half_adder_2 (.in_1(and_4_out), .in_2(and_5_out), .out_3(half_adder_2_out_3), .out_4(half_adder_2_out_4));
  Half_adder half_adder_3 (.in_1(and_9_out), .in_2(and_10_out), .out_3(half_adder_3_out_3), .out_4(half_adder_3_out_4));
  full_adder full_adder_3 (
    .in_1(and_11_out), .in_2(and_12_out), .in_3(full_adder_2_out_5), .out_4(full_adder_3_out_4),
    .out_5(full_adder_3_out_5));
  full_adder full_adder_4 (
    .in_1(full_adder_2_out_4), .in_2(half_adder_3_out_3), .in_3(full_adder_1_out_5), .out_4(out_12),
    .out_5(full_adder_4_out_5));
  full_adder full_adder_5 (
    .in_1(and_14_out), .in_2(and_15_out), .in_3(full_adder_3_out_5), .out_4(full_adder_5_out_4),
    .out_5(full_adder_5_out_5));
  full_adder full_adder_6 (
    .in_1(full_adder_4_out_5), .in_2(half_adder_3_out_4), .in_3(and_13_out), .out_4(full_adder_6_out_4),
    .out_5(full_adder_6_out_5));
  full_adder full_adder_7 (
    .in_1(half_adder_4_out_4), .in_2(full_adder_6_out_5), .in_3(full_adder_5_out_4), .out_4(out_14),
    .out_5(full_adder_7_out_5));
  Half_adder half_adder_4 (
    .in_1(full_adder_6_out_4), .in_2(full_adder_3_out_4), .out_3(out_13), .out_4(half_adder_4_out_4));
  full_adder full_adder_8 (
    .in_1(full_adder_7_out_5), .in_2(full_adder_5_out_5), .in_3(and_16_out), .out_4(out_15), .out_5(out_16));
endmodule

module _4_Bit_Divider (
  input  in_1,
  input  in_2,
  input  in_3,
  input  in_4,
  input  in_5,
  input  in_6,
  input  in_7,
  input  in_8
);

  wire and_1_out, and_2_out, and_3_out, and_4_out, and_5_out, and_6_out, and_7_out, and_8_out, and_9_out,
       clock_1_out, d_ff_1_qn, d_ff_2_q, d_ff_3_q, d_ff_4_q, d_ff_5_q, d_ff_6_q, d_ff_7_q, d_ff_8_q,
       or_1_out, or_2_out, or_3_out, or_4_out, or_5_out, or_6_out, or_7_out, or_8_out, or_9_out;

  Clock clock_1 (.out(clock_1_out));
  D_Flip_Flop d_ff_1 (.clk(clock_1_out), .Qn(d_ff_1_qn));  // open: D, Q, preset, en, reset
  and and_1 (and_1_out, d_ff_1_qn, in_1);
  buf or_1 (or_1_out, and_1_out);  // OR_Gate
  D_Flip_Flop d_ff_2 (.clk(clock_1_out), .D(or_1_out), .Q(d_ff_2_q));  // open: Qn, preset, en, reset
  and and_2 (and_2_out, d_ff_1_qn, in_2);
  buf or_2 (or_2_out, and_2_out);  // OR_Gate
  Multiplexer multiplexer_1 (.in0(d_ff_2_q), .in1(d_ff_3_q));  // open: out, sel, en
  D_Flip_Flop d_ff_3 (.clk(clock_1_out), .D(or_2_out), .Q(d_ff_3_q));  // open: Qn, preset, en, reset
  Multiplexer multiplexer_2 (.in0(d_ff_2_q), .in1(d_ff_4_q));  // open: out, sel, en
  and and_3 (and_3_out, d_ff_1_qn, in_3);
  buf or_3 (or_3_out, and_3_out);  // OR_Gate
  and and_4 (and_4_out, d_ff_1_qn, in_4);
  D_Flip_Flop d_ff_4 (.clk(clock_1_out), .D(or_3_out), .Q(d_ff_4_q));  // open: Qn, preset, en, reset
  buf or_4 (or_4_out, and_4_out);  // OR_Gate
  Multiplexer multiplexer_3 (.in0(d_ff_3_q), .in1(d_ff_5_q));  // open: out, sel, en
  D_Flip_Flop d_ff_5 (.clk(clock_1_out), .D(or_4_out), .Q(d_ff_5_q));  // open: Qn, preset, en, reset
  Multiplexer multiplexer_4 (.in0(d_ff_4_q), .in1(d_ff_6_q));  // open: out, sel, en
  and and_5 (and_5_out, d_ff_1_qn, in_5);
  buf or_5 (or_5_out, and_5_out);  // OR_Gate
  and and_6 (and_6_out, d_ff_1_qn, in_8);
  buf or_6 (or_6_out, and_6_out);  // OR_Gate
  D_Flip_Flop d_ff_6 (.clk(clock_1_out), .D(or_5_out), .Q(d_ff_6_q));  // open: Qn, preset, en, reset
  Multiplexer multiplexer_5 (.in0(d_ff_5_q), .in1(d_ff_7_q));  // open: out, sel, en
  and and_7 (and_7_out, d_ff_1_qn, in_6);
  buf or_7 (or_7_out, and_7_out);  // OR_Gate
  D_Flip_Flop d_ff_7 (.clk(clock_1_out), .D(or_6_out), .Q(d_ff_7_q));  // open: Qn, preset, en, reset
  Multiplexer multiplexer_6 (.in0(d_ff_6_q), .in1(d_ff_8_q));  // open: out, sel, en
  D_Flip_Flop d_ff_8 (.clk(clock_1_out), .D(or_7_out), .Q(d_ff_8_q));  // open: Qn, preset, en, reset
  and and_8 (and_8_out, d_ff_1_qn, in_7);
  buf or_8 (or_8_out, and_8_out);  // OR_Gate
  Multiplexer multiplexer_7 (.in0(d_ff_7_q));  // open: in1, out, sel, en
  buf and_9 (and_9_out, 1'b1);  // AND_Gate
  buf or_9 (or_9_out, and_9_out);  // OR_Gate
  D_Flip_Flop d_ff_9 (.clk(clock_1_out), .D(or_8_out));  // open: Q, Qn, preset, en, reset
  Multiplexer multiplexer_8 (.in0(d_ff_8_q));  // open: in1, out, sel, en
  D_Flip_Flop d_ff_10 (.clk(clock_1_out), .D(or_9_out));  // open: Q, Qn, preset, en, reset
endmodule

module Left_Shift (
  input  in_1,
  input  in_2,
  input  in_3,
  input  in_4,
  input  in_5,
  output out_6,
  output out_7,
  output out_8,
  output out_9
);

  wire and_1_out, and_2_out, and_3_out, and_4_out, and_5_out, and_6_out, and_7_out, and_8_out, not_1_out,
       not_2_out, not_3_out, not_4_out;

  not not_1 (not_1_out, in_1);
  not not_2 (not_2_out, in_1);
  not not_3 (not_3_out, in_1);
  not not_4 (not_4_out, in_1);
  and and_1 (and_1_out, 1'b0, in_1);
  and and_2 (and_2_out, not_2_out, in_2);
  and and_3 (and_3_out, in_1, in_2);
  and and_4 (and_4_out, not_3_out, in_3);
  and and_5 (and_5_out, in_1, in_3);
  and and_6 (and_6_out, not_4_out, in_4);
  and and_7 (and_7_out, in_1, in_4);
  and and_8 (and_8_out, not_1_out, in_5);
  or or_1 (out_6, and_1_out, and_2_out);
  or or_2 (out_7, and_3_out, and_4_out);
  or or_3 (out_8, and_5_out, and_6_out);
  or or_4 (out_9, and_7_out, and_8_out);
endmodule

module Right_shift (
  input  in_1,
  input  in_2,
  input  in_3,
  input  in_4,
  input  in_5,
  output out_6,
  output out_7,
  output out_8,
  output out_9
);

  wire and_1_out, and_2_out, and_3_out, and_4_out, and_5_out, and_6_out, and_7_out, and_8_out, not_1_out,
       not_2_out, not_3_out, not_4_out;

  not not_1 (not_1_out, in_1);
  not not_2 (not_2_out, in_1);
  not not_3 (not_3_out, in_1);
  not not_4 (not_4_out, in_1);
  and and_1 (and_1_out, not_1_out, in_2);
  and and_2 (and_2_out, in_1, in_3);
  and and_3 (and_3_out, not_2_out, in_3);
  and and_4 (and_4_out, in_1, in_4);
  and and_5 (and_5_out, not_3_out, in_4);
  and and_6 (and_6_out, in_1, in_5);
  and and_7 (and_7_out, not_4_out, in_5);
  and and_8 (and_8_out, in_1, 1'b0);
  or or_1 (out_6, and_1_out, and_2_out);
  or or_2 (out_7, and_3_out, and_4_out);
  or or_3 (out_8, and_5_out, and_6_out);
  or or_4 (out_9, and_7_out, and_8_out);
endmodule

module _4_Bit_comparator (
  input  A0,
  input  B0,
  input  A1,
  input  B1,
  input  A2,
  input  B2,
  input  A3,
  input  B3,
  output out_9,
  output out_10,
  output out_11
);

  wire and_1_out, and_2_out, and_3_out, and_4_out, and_5_out, and_6_out, and_7_out, and_8_out, not_1_out,
       not_2_out, not_3_out, not_4_out, not_5_out, not_6_out, not_7_out, not_8_out, xnor_1_out, xnor_2_out,
       xnor_3_out, xnor_4_out;

  not not_1 (not_1_out, B3);
  not not_2 (not_2_out, B2);
  not not_3 (not_3_out, B0);
  xnor xnor_1 (xnor_1_out, A0, B0);
  xnor xnor_2 (xnor_2_out, A1, B1);
  xnor xnor_3 (xnor_3_out, A2, B2);
  not not_4 (not_4_out, B1);
  not not_5 (not_5_out, A3);
  not not_6 (not_6_out, A2);
  not not_7 (not_7_out, A1);
  not not_8 (not_8_out, A0);
  xnor xnor_4 (xnor_4_out, A3, B3);
  and and_1 (and_1_out, A3, not_1_out);
  and and_2 (and_2_out, A2, not_2_out, xnor_4_out);
  and and_3 (and_3_out, xnor_4_out, xnor_3_out, A1, not_4_out);
  and and_4 (and_4_out, xnor_4_out, xnor_3_out, xnor_2_out, A0, not_3_out);
  and and_5 (and_5_out, not_5_out, B3);
  and and_6 (and_6_out, not_6_out, B2, xnor_4_out);
  and and_7 (and_7_out, xnor_4_out, xnor_3_out, not_7_out, B1);
  and and_8 (and_8_out, xnor_4_out, xnor_3_out, xnor_2_out, not_8_out, B0);
  and and_9 (out_9, xnor_1_out, xnor_2_out, xnor_3_out, xnor_4_out);
  or or_1 (out_10, and_1_out, and_2_out, and_3_out, and_4_out);
  or or_2 (out_11, and_5_out, and_6_out, and_7_out, and_8_out);
endmodule

module Bitwise_and (
  input  A3,
  input  B3,
  input  A2,
  input  B2,
  input  A1,
  input  B1,
  input  A0,
  input  B0,
  output out_9,
  output out_10,
  output out_11,
  output out_12
);

  and and_1 (out_9, A3, B3);
  and and_2 (out_10, A2, B2);
  and and_3 (out_11, A1, B1);
  and and_4 (out_12, A0, B0);
endmodule

module Bitsie_or (
  input  A3,
  input  B3,
  input  A2,
  input  B2,
  input  A1,
  input  B1,
  input  A0,
  input  B0,
  output out_9,
  output out_10,
  output out_11,
  output out_12
);

  or or_1 (out_9, A3, B3);
  or or_2 (out_10, A2, B2);
  or or_3 (out_11, A1, B1);
  or or_4 (out_12, A0, B0);
endmodule

module Bitwise_xor (
  input  A3,
  input  B3,
  input  A2,
  input  B2,
  input  A1,
  input  B1,
  input  A0,
  input  B0,
  output out_9,
  output out_10,
  output out_11,
  output out_12
);

  xor xor_1 (out_9, A3, B3);
  xor xor_2 (out_10, A2, B2);
  xor xor_3 (out_11, A1, B1);
  xor xor_4 (out_12, A0, B0);
endmodule

module Bitwise_not (
  input  in_1,
  input  in_2,
  input  in_3,
  input  in_4,
  output out_5,
  output out_6,
  output out_7,
  output out_8
);

  not not_1 (out_5, in_1);
  not not_2 (out_6, in_2);
  not not_3 (out_7, in_3);
  not not_4 (out_8, in_4);
endmodule
